// Logisim project Circuitos Aula.circ as structural Verilog
module Meio_Somador (
  input  A,
  input  B,
  output out_3,
  output out_4
);

  xor xor_1 (out_3, A, B);
  and and_1 (out_4, B, A);

  // Notes on the sheet:
  //   Meio Somador
endmodule

module Somador (
  input  Cin,
  input  A,
  input  B,
  output S,
  output Ts
);

  wire meio_somador_1_out_3, meio_somador_1_out_4, meio_somador_2_out_4;

  Meio_Somador meio_somador_1 (.A(A), .B(B), .out_3(meio_somador_1_out_3), .out_4(meio_somador_1_out_4));
  Meio_Somador meio_somador_2 (.A(Cin), .B(meio_somador_1_out_3), .out_3(S), .out_4(meio_somador_2_out_4));
  or or_1 (Ts, meio_somador_2_out_4, meio_somador_1_out_4);
endmodule

module Somador_4_bits (
  input  TE,
  input  A1,
  input  B1,
  input  A2,
  input  B2,
  input  A3,
  input  B3,
  input  A4,
  input  B4,
  output S1,
  output S2,
  output S3,
  output S4,
  output Carry_Out
);

  wire somador_1_ts, somador_2_ts, somador_3_ts;

  Somador somador_1 (.Cin(TE), .A(A1), .B(B1), .S(S1), .Ts(somador_1_ts));
  Somador somador_2 (.Cin(somador_1_ts), .A(A2), .B(B2), .S(S2), .Ts(somador_2_ts));
  Somador somador_3 (.Cin(somador_2_ts), .A(A3), .B(B3), .S(S3), .Ts(somador_3_ts));
  Somador somador_4 (.Cin(somador_3_ts), .A(A4), .B(B4), .S(S4), .Ts(Carry_Out));
  LED led_1 (.in(Carry_Out));

  // Notes on the sheet:
  //   Overflow
  //   Somador de 4 Bits
endmodule

module Somador_8_Bits (
  input  Cin,
  input  A0,
  input  B0,
  input  A1,
  input  B1,
  input  A2,
  input  B2,
  input  A3,
  input  A4,
  input  B3,
  input  B4,
  input  A5,
  input  B5,
  input  A6,
  input  B6,
  input  A7,
  input  B7,
  output S0,
  output S1,
  output S2,
  output S3,
  output S4,
  output S5,
  output S6,
  output S7
);

  wire somador_4_bits_1_carry_out, somador_4_bits_2_carry_out;

  Somador_4_bits somador_4_bits_1 (
    .TE(Cin), .A1(A0), .B1(B0), .A2(A1), .B2(B1), .A3(A2), .B3(B2), .A4(A3), .B4(B3), .S1(S0), .S2(S1),
    .S3(S2), .S4(S3), .Carry_Out(somador_4_bits_1_carry_out));
  Somador_4_bits somador_4_bits_2 (
    .TE(somador_4_bits_1_carry_out), .A1(A4), .B1(B4), .A2(A5), .B2(B5), .A3(A6), .B3(B6), .A4(A7), .B4(B7),
    .S1(S4), .S2(S5), .S3(S6), .S4(S7), .Carry_Out(somador_4_bits_2_carry_out));
  LED led_1 (.in(somador_4_bits_2_carry_out));

  // Notes on the sheet:
  //   Somador de 8 Bits
  //   TS
  //   Overflow
endmodule
